// Digital circuit MITE_16bit_Sept1.dig as structural Verilog
module MITE_16bit_Sept1 (
  input  clk,
  input  in_2,
  input  in_3,
  input  in_4,
  output LD,
  output RES,
  output GCLK,
  output T0,
  output nRST
);

  wire ADD, AND, Aout, Bout, BUS1, BUS2, BUS3, BUS4, BUS5, BUS6, BUS7, BUS8, BUS9, BUS10, BUS11, BUS12,
       BUS13, BUS14, BUS15, button_1_out, button_2_out, button_3_out, button_4_out, button_5_out,
       button_6_out, button_7_out, button_8_out, button_9_out, button_10_out, button_11_out, button_12_out,
       button_13_out, button_14_out, button_15_out, button_16_out, button_17_out, C, Cin, CLA, CLR, Cout, D0,
       D1, D2, D3, D4, D5, D6, D7, D8, D9, D10, D11, D12, D13, D14, D15, d_ff_1_nq, d_ff_2_nq, d_ff_3_nq,
       d_ff_4_nq, d_ff_5_nq, d_ff_6_nq, d_ff_7_nq, d_ff_8_nq, d_ff_9_nq, d_ff_10_nq, d_ff_11_nq, d_ff_12_nq,
       diodebackward_1_out, diodebackward_2_out, diodebackward_8_out, diodebackward_9_out,
       diodebackward_20_out, diodebackward_26_out, diodeforward_1_out, diodeforward_17_out,
       diodeforward_19_out, F, Fout, I0, I1, IC17_2_nq, IC17_3_nq, IC17_4_nq, IC17_nq, IX, LD_t, LOAD, nA,
       nand_1_out, nand_2_out, nand_3_out, nand_4_out, nand_6_out, nand_8_out, nand_10_out, nand_11_out,
       nand_14_out, nand_16_out, nand_17_out, nand_18_out, nand_19_out, nand_20_out, nand_21_out, nB, nJMP,
       not_1_out, not_2_out, not_3_out, not_4_out, not_7_out, not_8_out, not_9_out, nRESET, OR, PC_Cin,
       PC_Cout, PC_S, PCin, PCout, pullup_2_out, pullup_4_out, pullup_7_out, pullup_8_out, pullup_9_out,
       pullup_11_out, pullup_13_out, RCO, RST, SETC, ST, SUB, U4_pin9, U6_pin9, U10_pin15, XOR, xor_1_out,
       xor_2_out, xor_3_out, xor_4_out, ZERO;
  wire [3:0] U5_pin3, U5_pin7, U6_pin3, U6_pin7, U10_pin11;

  nand nand_1 (nand_1_out, T0, nand_4_out, nand_2_out);
  nand nand_2 (nand_2_out, nand_1_out, GCLK, nRESET);
  nand nand_3 (nand_3_out, nand_2_out, GCLK, nand_4_out);
  nand nand_4 (nand_4_out, nand_3_out, PC_Cout, nRESET);
  _74595 U6 (
    .pin1(U6_pin3[2]), .pin2(U6_pin3[1]), .pin3(U6_pin3[0]), .pin4(U6_pin7[3]), .pin5(U6_pin7[2]),
    .pin6(U6_pin7[1]), .pin7(U6_pin7[0]), .pin8(1'b0), .pin9(U6_pin9), .pin10(nRESET), .pin11(GCLK),
    .pin12(T0), .pin13(1'b0), .pin14(PCin), .pin15(U6_pin3[3]), .pin16(1'b1));
  _74138 U1 (
    .pin1(in_2), .pin2(in_3), .pin3(in_4), .pin4(1'b0), .pin5(1'b0), .pin6(1'b1), .pin7(nJMP), .pin8(1'b0),
    .pin9(ST), .pin10(SUB), .pin11(ADD), .pin12(XOR), .pin13(OR), .pin14(AND), .pin15(LOAD), .pin16(1'b1));
  nand nand_5 (PC_Cin, T0, nand_2_out, nand_6_out);
  nand nand_6 (nand_6_out, PC_Cin, nand_3_out, nRESET);
  DiodeBackward diodebackward_1 (.in(LOAD), .out(diodebackward_1_out));
  PullUp pullup_1 (.out(diodebackward_1_out));
  DiodeBackward diodebackward_2 (.in(LOAD), .out(diodebackward_2_out));
  DiodeBackward diodebackward_3 (.in(ADD), .out(diodebackward_2_out));
  DiodeBackward diodebackward_4 (.in(SUB), .out(diodebackward_2_out));
  DiodeBackward diodebackward_5 (.in(nJMP), .out(diodebackward_2_out));
  _74595 U5 (
    .pin1(U5_pin3[2]), .pin2(U5_pin3[1]), .pin3(U5_pin3[0]), .pin4(U5_pin7[3]), .pin5(U5_pin7[2]),
    .pin6(U5_pin7[1]), .pin7(U5_pin7[0]), .pin8(1'b0), .pin9(PCout), .pin10(nRESET), .pin11(GCLK),
    .pin12(T0), .pin13(1'b0), .pin14(U6_pin9), .pin15(U5_pin3[3]), .pin16(1'b1));
  PullUp pullup_2 (.out(pullup_2_out));
  PullUp pullup_3 (.out(diodebackward_2_out));
  DiodeBackward diodebackward_6 (.in(SUB), .out(pullup_2_out));
  PullUp pullup_4 (.out(pullup_4_out));
  DiodeBackward diodebackward_7 (.in(SUB), .out(pullup_4_out));
  DiodeBackward diodebackward_8 (.in(nJMP), .out(diodebackward_8_out));
  PullUp pullup_5 (.out(diodebackward_8_out));
  DiodeBackward diodebackward_9 (.in(AND), .out(diodebackward_9_out));
  DiodeBackward diodebackward_10 (.in(OR), .out(diodebackward_9_out));
  PullUp pullup_6 (.out(diodebackward_9_out));
  PullUp pullup_7 (.out(pullup_7_out));
  DiodeBackward diodebackward_11 (.in(LOAD), .out(pullup_7_out));
  DiodeBackward diodebackward_12 (.in(OR), .out(pullup_7_out));
  DiodeBackward diodebackward_13 (.in(XOR), .out(pullup_7_out));
  DiodeBackward diodebackward_14 (.in(ADD), .out(pullup_7_out));
  DiodeBackward diodebackward_15 (.in(SUB), .out(pullup_7_out));
  DiodeBackward diodebackward_16 (.in(ST), .out(pullup_7_out));
  DiodeBackward diodebackward_17 (.in(nJMP), .out(pullup_7_out));
  _74540 U2 (
    .pin1(1'b0), .pin2(pullup_7_out), .pin3(diodebackward_9_out), .pin4(diodebackward_8_out),
    .pin5(pullup_4_out), .pin6(pullup_2_out), .pin7(diodebackward_2_out), .pin8(diodebackward_1_out),
    .pin9(1'b0), .pin10(1'b0), .pin12(CLA), .pin13(F), .pin14(C), .pin15(nB), .pin16(nA), .pin17(I1),
    .pin18(I0), .pin19(1'b0), .pin20(1'b1));  // open: pin11
  Seven_Seg_Hex seven_seg_hex_1 (.d(U6_pin3), .dp(1'b0));
  Seven_Seg_Hex seven_seg_hex_2 (.d(U6_pin7), .dp(1'b0));
  Seven_Seg_Hex seven_seg_hex_3 (.d(U5_pin3), .dp(1'b0));
  DiodeForward diodeforward_1 (.in(BUS15), .out(diodeforward_1_out));
  DiodeForward diodeforward_2 (.in(BUS14), .out(diodeforward_1_out));
  DiodeForward diodeforward_3 (.in(BUS13), .out(diodeforward_1_out));
  DiodeForward diodeforward_4 (.in(BUS12), .out(diodeforward_1_out));
  DiodeForward diodeforward_5 (.in(BUS11), .out(diodeforward_1_out));
  DiodeForward diodeforward_6 (.in(BUS10), .out(diodeforward_1_out));
  DiodeForward diodeforward_7 (.in(BUS9), .out(diodeforward_1_out));
  DiodeForward diodeforward_8 (.in(BUS8), .out(diodeforward_1_out));
  DiodeForward diodeforward_9 (.in(BUS7), .out(diodeforward_1_out));
  DiodeForward diodeforward_10 (.in(BUS6), .out(diodeforward_1_out));
  DiodeForward diodeforward_11 (.in(BUS5), .out(diodeforward_1_out));
  DiodeForward diodeforward_12 (.in(BUS4), .out(diodeforward_1_out));
  DiodeForward diodeforward_13 (.in(BUS3), .out(diodeforward_1_out));
  DiodeForward diodeforward_14 (.in(BUS2), .out(diodeforward_1_out));
  DiodeForward diodeforward_15 (.in(BUS1), .out(diodeforward_1_out));
  DiodeForward diodeforward_16 (.in(Aout), .out(diodeforward_1_out));
  Reset reset_1 (.out(nRESET));
  Monoflop monoflop_1 (.C(LD), .R(1'b0), .Q(SETC), .nQ(RES));
  Monoflop monoflop_2 (.C(button_1_out), .R(1'b0), .Q(LD_t), .nQ(LD));
  Button button_1 (.out(button_1_out));
  Seven_Seg_Hex seven_seg_hex_4 (.d(U5_pin7), .dp(1'b0));
  nand nand_7 (ZERO, diodeforward_1_out, diodeforward_1_out);
  PullDown pulldown_1 (.out(diodeforward_1_out));
  LED led_1 (.in(D15));
  D_FF IC17 (.D(IC17_nq), .C(button_2_out), .Q(D15), .nQ(IC17_nq));
  LED led_2 (.in(D14));
  D_FF d_ff_1 (.D(d_ff_1_nq), .C(button_3_out), .Q(D14), .nQ(d_ff_1_nq));
  Button button_2 (.out(button_2_out));
  LED led_3 (.in(D13));
  D_FF d_ff_2 (.D(d_ff_2_nq), .C(button_4_out), .Q(D13), .nQ(d_ff_2_nq));
  Button button_3 (.out(button_3_out));
  LED led_4 (.in(D12));
  D_FF d_ff_3 (.D(d_ff_3_nq), .C(button_5_out), .Q(D12), .nQ(d_ff_3_nq));
  Button button_4 (.out(button_4_out));
  _74164 U7 (
    .pin1(1'b1), .pin2(Fout), .pin3(BUS15), .pin4(BUS14), .pin5(BUS13), .pin6(BUS12), .pin7(1'b0),
    .pin8(GCLK), .pin9(CLR), .pin10(BUS11), .pin11(BUS10), .pin12(BUS9), .pin13(BUS8), .pin14(1'b1));
  _74165 U4 (
    .pin1(LD), .pin2(GCLK), .pin3(D7), .pin4(D6), .pin5(D5), .pin6(D4), .pin8(1'b0), .pin9(U4_pin9),
    .pin10(1'b0), .pin11(D15), .pin12(D14), .pin13(D13), .pin14(D12), .pin15(1'b0), .pin16(1'b1));  // open: pin7
  LED led_5 (.in(D11));
  D_FF d_ff_4 (.D(d_ff_4_nq), .C(button_6_out), .Q(D11), .nQ(d_ff_4_nq));
  Button button_5 (.out(button_5_out));
  LED led_6 (.in(D10));
  D_FF d_ff_5 (.D(d_ff_5_nq), .C(button_7_out), .Q(D10), .nQ(d_ff_5_nq));
  Button button_6 (.out(button_6_out));
  Seven_Seg_Hex seven_seg_hex_5 (.d({BUS15, BUS14, BUS13, BUS12}), .dp(1'b0));
  Seven_Seg_Hex seven_seg_hex_6 (.d({D15, D14, D13, D12}), .dp(1'b0));
  LED led_7 (.in(D9));
  D_FF d_ff_6 (.D(d_ff_6_nq), .C(button_8_out), .Q(D9), .nQ(d_ff_6_nq));
  Button button_7 (.out(button_7_out));
  Seven_Seg_Hex seven_seg_hex_7 (.d({BUS11, BUS10, BUS9, BUS8}), .dp(1'b0));
  Seven_Seg_Hex seven_seg_hex_8 (.d({D11, D10, D9, D8}), .dp(1'b0));
  LED led_8 (.in(D8));
  D_FF IC17_2 (.D(IC17_2_nq), .C(button_9_out), .Q(D8), .nQ(IC17_2_nq));
  Button button_8 (.out(button_8_out));
  Seven_Seg_Hex seven_seg_hex_9 (.d({BUS7, BUS6, BUS5, BUS4}), .dp(1'b0));
  _74165 U3 (
    .pin1(LD), .pin2(GCLK), .pin3(D3), .pin4(D2), .pin5(D1), .pin6(D0), .pin8(1'b0), .pin9(Bout),
    .pin10(U4_pin9), .pin11(D7), .pin12(D6), .pin13(D5), .pin14(D4), .pin15(1'b0), .pin16(1'b1));  // open: pin7
  Seven_Seg_Hex seven_seg_hex_10 (.d({D7, D6, D5, D4}), .dp(1'b0));
  LED led_9 (.in(D7));
  D_FF IC17_3 (.D(IC17_3_nq), .C(button_10_out), .Q(D7), .nQ(IC17_3_nq));
  Button button_9 (.out(button_9_out));
  Seven_Seg_Hex seven_seg_hex_11 (.d({BUS3, BUS2, BUS1, Aout}), .dp(1'b0));
  _74164 U8 (
    .pin1(1'b1), .pin2(BUS8), .pin3(BUS7), .pin4(BUS6), .pin5(BUS5), .pin6(BUS4), .pin7(1'b0), .pin8(GCLK),
    .pin9(CLR), .pin10(BUS3), .pin11(BUS2), .pin12(BUS1), .pin13(Aout), .pin14(1'b1));
  Seven_Seg_Hex seven_seg_hex_12 (.d({D3, D2, D1, D0}), .dp(1'b0));
  LED led_10 (.in(D6));
  D_FF d_ff_7 (.D(d_ff_7_nq), .C(button_11_out), .Q(D6), .nQ(d_ff_7_nq));
  Button button_10 (.out(button_10_out));
  LED led_11 (.in(D5));
  D_FF d_ff_8 (.D(d_ff_8_nq), .C(button_12_out), .Q(D5), .nQ(d_ff_8_nq));
  Button button_11 (.out(button_11_out));
  LED led_12 (.in(D4));
  D_FF d_ff_9 (.D(d_ff_9_nq), .C(button_13_out), .Q(D4), .nQ(d_ff_9_nq));
  Button button_12 (.out(button_12_out));
  LED led_13 (.in(D3));
  D_FF d_ff_10 (.D(d_ff_10_nq), .C(button_14_out), .Q(D3), .nQ(d_ff_10_nq));
  Button button_13 (.out(button_13_out));
  LED led_14 (.in(D2));
  D_FF d_ff_11 (.D(d_ff_11_nq), .C(button_15_out), .Q(D2), .nQ(d_ff_11_nq));
  Button button_14 (.out(button_14_out));
  LED led_15 (.in(D1));
  D_FF d_ff_12 (.D(d_ff_12_nq), .C(button_16_out), .Q(D1), .nQ(d_ff_12_nq));
  Button button_15 (.out(button_15_out));
  LED led_16 (.in(D0));
  D_FF IC17_4 (.D(IC17_4_nq), .C(button_17_out), .Q(D0), .nQ(IC17_4_nq));
  Button button_16 (.out(button_16_out));
  Button button_17 (.out(button_17_out));
  xor xor_1 (xor_1_out, Aout, nA);
  xor xor_2 (xor_2_out, nB, Bout);
  nand nand_8 (nand_8_out, SETC, C);
  nand nand_9 (CLR, CLA, LD_t);
  not not_1 (not_1_out, PCout);
  not not_2 (not_2_out, PC_Cin);
  nand nand_10 (nand_10_out, C, C);
  nand nand_11 (nand_11_out, clk, clk);
  nand nand_12 (RST, RES, nRST);
  nand nand_13 (nRST, RST, T0);
  nand nand_14 (nand_14_out, nand_10_out, LD_t);
  PullUp pullup_8 (.out(pullup_8_out));
  DiodeBackward diodebackward_18 (.in(not_1_out), .out(pullup_8_out));
  DiodeBackward diodebackward_19 (.in(PC_Cin), .out(pullup_8_out));
  DiodeBackward diodebackward_20 (.in(not_2_out), .out(diodebackward_20_out));
  DiodeBackward diodebackward_21 (.in(PCout), .out(diodebackward_20_out));
  PullUp pullup_9 (.out(pullup_9_out));
  DiodeBackward diodebackward_22 (.in(PC_Cin), .out(pullup_9_out));
  DiodeBackward diodebackward_23 (.in(PCout), .out(pullup_9_out));
  xor xor_3 (xor_3_out, xor_1_out, xor_2_out);
  nand nand_15 (GCLK, nand_11_out, RST);
  PullUp pullup_10 (.out(diodebackward_20_out));
  DiodeForward diodeforward_17 (.in(pullup_8_out), .out(diodeforward_17_out));
  DiodeForward diodeforward_18 (.in(diodebackward_20_out), .out(diodeforward_17_out));
  DiodeForward diodeforward_19 (.in(pullup_9_out), .out(diodeforward_19_out));
  not not_3 (not_3_out, diodeforward_17_out);
  PullDown pulldown_2 (.out(diodeforward_17_out));
  not not_4 (not_4_out, diodeforward_19_out);
  PullDown pulldown_3 (.out(diodeforward_19_out));
  xor xor_4 (xor_4_out, xor_3_out, Cin);
  nand nand_16 (nand_16_out, xor_3_out, Cin);
  nand nand_17 (nand_17_out, xor_1_out, xor_2_out);
  not not_5 (PC_S, not_3_out);
  not not_6 (PC_Cout, not_4_out);
  nand nand_18 (nand_18_out, nand_16_out, nand_17_out);
  _74161 U10 (
    .pin1(RST), .pin2(clk), .pin3(1'b0), .pin4(1'b0), .pin5(1'b0), .pin6(1'b0), .pin7(1'b1), .pin8(1'b0),
    .pin9(1'b1), .pin10(1'b1), .pin11(U10_pin11[3]), .pin12(U10_pin11[2]), .pin13(U10_pin11[1]),
    .pin14(U10_pin11[0]), .pin15(U10_pin15), .pin16(1'b1));
  nand nand_19 (nand_19_out, xor_4_out, I0);
  nand nand_20 (nand_20_out, I1, nand_18_out);
  nand nand_21 (nand_21_out, nand_18_out, F);
  not not_7 (not_7_out, nJMP);
  nand nand_22 (Fout, nand_19_out, nand_20_out);
  nand nand_23 (Cout, nand_21_out, nand_21_out);
  Seven_Seg_Hex seven_seg_hex_13 (.d(U10_pin11), .dp(1'b0));
  and and_1 (RCO, U10_pin11[2], U10_pin11[1], U10_pin11[0], U10_pin11[3]);
  PullUp pullup_11 (.out(pullup_11_out));
  DiodeBackward diodebackward_24 (.in(PC_S), .out(pullup_11_out));
  DiodeBackward diodebackward_25 (.in(nJMP), .out(pullup_11_out));
  DiodeBackward diodebackward_26 (.in(not_7_out), .out(diodebackward_26_out));
  DiodeBackward diodebackward_27 (.in(Bout), .out(diodebackward_26_out));
  PullUp pullup_12 (.out(diodebackward_26_out));
  not not_8 (not_8_out, pullup_11_out);
  not not_9 (not_9_out, diodebackward_26_out);
  PullUp pullup_13 (.out(pullup_13_out));
  DiodeBackward diodebackward_28 (.in(not_8_out), .out(pullup_13_out));
  not not_10 (PCin, pullup_13_out);
  DiodeBackward diodebackward_29 (.in(not_9_out), .out(pullup_13_out));
  _7474 U12 (
    .pin1(nand_14_out), .pin2(Cout), .pin3(GCLK), .pin4(nand_8_out), .pin5(Cin), .pin7(1'b0), .pin8(T0),
    .pin9(IX), .pin10(1'b1), .pin11(clk), .pin12(RCO), .pin13(1'b1), .pin14(1'b1));  // open: pin6
  LED led_17 (.in(Cin));

  // Other names for the same wires on the sheet: BUS0 = Aout; nLOAD = LD; nRES = RES

  // Notes on the sheet:
  //   clk: Hz: 2147483647
  //   MITE
  //   PC FF
  //   Enter 3-bit Instruction
  //   100 = ADD
  //   101 = SUB
  //   Instruction Input
  //   Instruction Decode
  //   F
  //   CLA
  //   C
  //   ~B
  //   I1
  //   ~A
  //   I0
  //   PROGRAM COUNTER
  //   LOAD
  //   AND
  //   OR
  //   XOR
  //   ADD
  //   SUB
  //   STORE
  //   JMP
  //   STEP/RUN
  //   ZERO DETECT
  //   ENTER H
  //   16-bit Shift Register A
  //   16-bit Shift Register B
  //   AC / BUS
  //   B-REG
  //   Data Input
  //   ENTER L
  //   U9
  //   ALU
  //   CLR ACC
  //   MITE 16-bit  Bit serial CPU Testbed
  //   PC Incrementer and Jump Logic
  //   Carry is only set before Bit 0 of an operation
  //   Any residual carry is cleared before an operation
  //   Clock Sequencer
  //   Suppress Carry
  //   # Clock
  //   Carry FF
  //   CARRY
endmodule
