// Digital circuit discrete_flipflop_1.dig as structural Verilog
module discrete_flipflop_1 (
  output Q,
  output nQ
);

  wire CLK, DATA, nand_1_out, nand_2_out, nand_3_out, nand_4_out, nRST, nSET;

  nand nand_1 (nand_1_out, nSET, nand_4_out, nand_2_out);
  nand nand_2 (nand_2_out, nand_1_out, CLK, nRST);
  nand nand_3 (nand_3_out, nand_2_out, CLK, nand_4_out);
  nand nand_4 (nand_4_out, nand_3_out, DATA, nRST);
  nand nand_5 (Q, nSET, nand_2_out, nQ);
  nand nand_6 (nQ, Q, nand_3_out, nRST);

  // Notes on the sheet:
  //   ~SET
  //   CLOCK
  //   DATA
  //   ~RESET
  //   1
  //   2
  //   3
  //   4
  //   5
  //   6
endmodule
