// Digital circuit miteaugust25_1.dig as structural Verilog
module miteaugust25_1 (
  input  clk,
  input  in_2,
  input  in_3,
  input  in_4,
  output LD,
  output RES,
  output GCLK,
  output Sum,
  output Cout
);

  wire ADD, AND, Aout, Bin, BUS0, BUS1, BUS2, BUS3, BUS4, BUS5, BUS6, BUS7, button_1_out, button_2_out,
       button_3_out, button_4_out, button_5_out, button_6_out, button_7_out, button_8_out, button_9_out, C,
       C_t, Cin, CLA, CLR, Cout_t, D0, D1, D2, D3, D4, D5, D6, D7, d_ff_1_nq, d_ff_2_nq, d_ff_3_nq,
       d_ff_4_nq, d_ff_5_nq, d_ff_6_nq, diodebackward_1_out, diodebackward_4_out, diodebackward_7_out,
       diodebackward_10_out, diodebackward_13_out, diodebackward_16_out, diodebackward_19_out,
       diodebackward_22_out, diodebackward_25_out, diodebackward_30_out, diodebackward_32_out,
       diodebackward_33_out, diodebackward_35_out, diodebackward_44_out, diodebackward_46_out,
       diodebackward_61_out, diodebackward_66_out, diodebackward_71_out, diodebackward_75_out,
       diodebackward_77_out, diodebackward_80_out, diodebackward_85_out, diodebackward_92_out,
       diodebackward_94_out, diodebackward_96_out, diodebackward_101_out, diodebackward_103_out,
       diodebackward_105_out, diodebackward_107_out, diodebackward_109_out, diodebackward_111_out,
       diodebackward_112_out, diodebackward_114_out, diodebackward_116_out, diodebackward_118_out,
       diodebackward_120_out, diodeforward_1_out, diodeforward_9_out, diodeforward_11_out,
       diodeforward_15_out, diodeforward_18_out, diodeforward_20_out, diodeforward_22_out,
       diodeforward_23_out, diodeforward_25_out, F, Fout, GATE, I0, I1, IC16_2_nq, IC16_nq, IX, LD_t, LOAD,
       nA, nand_1_out, nand_2_out, nand_3_out, nand_4_out, nand_5_out, nand_6_out, nand_7_out, nand_8_out,
       nand_10_out, nand_12_out, nand_13_out, nand_14_out, nand_15_out, nand_16_out, nand_17_out,
       nand_18_out, nand_19_out, nand_20_out, nand_22_out, nand_24_out, nand_25_out, nand_26_out,
       nand_27_out, nand_28_out, nand_29_out, nand_30_out, nand_31_out, nand_32_out, nand_34_out,
       nand_36_out, nand_37_out, nand_38_out, nand_39_out, nand_40_out, nand_41_out, nand_42_out,
       nand_43_out, nand_44_out, nand_46_out, nand_48_out, nand_49_out, nand_50_out, nand_51_out,
       nand_52_out, nand_53_out, nand_54_out, nand_55_out, nand_56_out, nand_58_out, nand_60_out,
       nand_61_out, nand_65_out, nand_66_out, nand_67_out, nand_68_out, nand_69_out, nand_70_out,
       nand_71_out, nand_72_out, nand_74_out, nand_76_out, nand_77_out, nand_78_out, nand_79_out,
       nand_80_out, nand_81_out, nand_82_out, nand_83_out, nand_84_out, nand_85_out, nand_86_out,
       nand_87_out, nand_88_out, nand_92_out, nand_94_out, nand_95_out, nand_96_out, nand_97_out,
       nand_98_out, nand_99_out, nand_100_out, nand_101_out, nand_102_out, nand_103_out, nand_104_out,
       nand_105_out, nand_106_out, nand_110_out, nand_112_out, nand_113_out, nand_114_out, nand_115_out,
       nand_116_out, nand_119_out, nand_120_out, nand_121_out, nand_122_out, nand_124_out, nand_125_out,
       nand_126_out, nand_127_out, nand_128_out, nand_129_out, nand_131_out, nand_133_out, nand_134_out,
       nand_135_out, nand_136_out, nand_138_out, nand_139_out, nand_140_out, nand_141_out, nand_142_out, nB,
       nC, nCRES, nCSET, nGATE, nIR4, nIR5, nIR6, nJMP, not_23_out, not_24_out, not_25_out, not_26_out,
       not_32_out, not_33_out, not_36_out, not_37_out, not_38_out, not_39_out, not_41_out, not_42_out,
       not_43_out, not_44_out, not_48_out, nRESET, nS0, nS1, nS2, nT0, OR, PC_Cin, PC_Cout, PC_S, PCin,
       PCout, pullup_10_out, pullup_17_out, pullup_18_out, pullup_19_out, pullup_20_out, pullup_29_out,
       pullup_30_out, RCO, S, S0, S1, S2, SETC, ST, SUB, T0, U4_pin9, XOR, ZERO;
  wire [3:0] nand_45_out, nand_47_out;
  wire [3:1] nand_57_out, nand_59_out;
  wire [3:3] nand_123_out;

  DiodeBackward diodebackward_1 (.in(nIR4), .out(diodebackward_1_out));
  DiodeBackward diodebackward_2 (.in(nIR5), .out(diodebackward_1_out));
  DiodeBackward diodebackward_3 (.in(nIR6), .out(diodebackward_1_out));
  DiodeBackward diodebackward_4 (.in(in_2), .out(diodebackward_4_out));
  DiodeBackward diodebackward_5 (.in(nIR6), .out(diodebackward_4_out));
  DiodeBackward diodebackward_6 (.in(nIR5), .out(diodebackward_4_out));
  DiodeBackward diodebackward_7 (.in(nIR4), .out(diodebackward_7_out));
  DiodeBackward diodebackward_8 (.in(in_3), .out(diodebackward_7_out));
  DiodeBackward diodebackward_9 (.in(nIR6), .out(diodebackward_7_out));
  DiodeBackward diodebackward_10 (.in(in_2), .out(diodebackward_10_out));
  DiodeBackward diodebackward_11 (.in(in_3), .out(diodebackward_10_out));
  DiodeBackward diodebackward_12 (.in(nIR6), .out(diodebackward_10_out));
  DiodeBackward diodebackward_13 (.in(nIR5), .out(diodebackward_13_out));
  DiodeBackward diodebackward_14 (.in(nIR4), .out(diodebackward_13_out));
  DiodeBackward diodebackward_15 (.in(in_4), .out(diodebackward_13_out));
  DiodeBackward diodebackward_16 (.in(in_2), .out(diodebackward_16_out));
  DiodeBackward diodebackward_17 (.in(nIR5), .out(diodebackward_16_out));
  DiodeBackward diodebackward_18 (.in(in_4), .out(diodebackward_16_out));
  DiodeBackward diodebackward_19 (.in(in_2), .out(diodebackward_19_out));
  DiodeBackward diodebackward_20 (.in(in_3), .out(diodebackward_19_out));
  DiodeBackward diodebackward_21 (.in(in_4), .out(diodebackward_19_out));
  DiodeBackward diodebackward_22 (.in(in_2), .out(diodebackward_22_out));
  DiodeBackward diodebackward_23 (.in(in_3), .out(diodebackward_22_out));
  DiodeBackward diodebackward_24 (.in(in_4), .out(diodebackward_22_out));
  not not_1 (nIR6, in_4);
  not not_2 (nIR5, in_3);
  not not_3 (nIR4, in_2);
  not not_4 (nT0, T0);
  nand nand_1 (nand_1_out, 1'b1, nand_4_out, nand_2_out);
  nand nand_2 (nand_2_out, nand_1_out, GCLK, nRESET);
  nand nand_3 (nand_3_out, nand_2_out, GCLK, nand_4_out);
  nand nand_4 (nand_4_out, nand_3_out, PCin, nRESET);
  nand nand_5 (nand_5_out, 1'b1, nand_8_out, nand_6_out);
  nand nand_6 (nand_6_out, nand_5_out, GCLK, CLR);
  nand nand_7 (nand_7_out, nand_6_out, GCLK, nand_8_out);
  nand nand_8 (nand_8_out, nand_7_out, Fout, CLR);
  DiodeBackward diodebackward_25 (.in(S2), .out(diodebackward_25_out));
  DiodeBackward diodebackward_26 (.in(1'b1), .out(diodebackward_25_out));
  PullUp pullup_1 (.out(diodebackward_1_out));
  not not_5 (LOAD, diodebackward_1_out);
  PullUp pullup_2 (.out(diodebackward_4_out));
  not not_6 (AND, diodebackward_4_out);
  PullUp pullup_3 (.out(diodebackward_7_out));
  not not_7 (OR, diodebackward_7_out);
  PullUp pullup_4 (.out(diodebackward_10_out));
  not not_8 (XOR, diodebackward_10_out);
  PullUp pullup_5 (.out(diodebackward_13_out));
  not not_9 (ADD, diodebackward_13_out);
  PullUp pullup_6 (.out(diodebackward_16_out));
  not not_10 (SUB, diodebackward_16_out);
  PullUp pullup_7 (.out(diodebackward_19_out));
  not not_11 (ST, diodebackward_19_out);
  PullUp pullup_8 (.out(diodebackward_22_out));
  not not_12 (nJMP, diodebackward_22_out);
  DiodeBackward diodebackward_27 (.in(D7), .out(diodebackward_25_out));
  DiodeBackward diodebackward_28 (.in(S1), .out(diodebackward_25_out));
  nand nand_9 (nand_45_out[3], 1'b1, nand_2_out, nand_10_out);
  nand nand_10 (nand_10_out, nand_45_out[3], nand_3_out, nRESET);
  nand nand_11 (nand_47_out[3], 1'b1, nand_6_out, nand_12_out);
  nand nand_12 (nand_12_out, nand_47_out[3], nand_7_out, CLR);
  DiodeBackward diodebackward_29 (.in(S0), .out(diodebackward_25_out));
  PullUp pullup_9 (.out(diodebackward_25_out));
  DiodeBackward diodebackward_30 (.in(S2), .out(diodebackward_30_out));
  DiodeBackward diodebackward_31 (.in(1'b1), .out(diodebackward_30_out));
  DiodeBackward diodebackward_32 (.in(LOAD), .out(diodebackward_32_out));
  DiodeBackward diodebackward_33 (.in(C_t), .out(diodebackward_33_out));
  DiodeBackward diodebackward_34 (.in(SETC), .out(diodebackward_33_out));
  DiodeBackward diodebackward_35 (.in(nC), .out(diodebackward_35_out));
  DiodeBackward diodebackward_36 (.in(LD_t), .out(diodebackward_35_out));
  DiodeBackward diodebackward_37 (.in(D6), .out(diodebackward_30_out));
  DiodeBackward diodebackward_38 (.in(S1), .out(diodebackward_30_out));
  PullUp pullup_10 (.out(pullup_10_out));
  PullUp pullup_11 (.out(diodebackward_32_out));
  DiodeBackward diodebackward_39 (.in(LOAD), .out(pullup_10_out));
  DiodeBackward diodebackward_40 (.in(ADD), .out(pullup_10_out));
  DiodeBackward diodebackward_41 (.in(SUB), .out(pullup_10_out));
  DiodeBackward diodebackward_42 (.in(nJMP), .out(pullup_10_out));
  PullUp pullup_12 (.out(diodebackward_33_out));
  not not_13 (nCSET, diodebackward_33_out);
  PullUp pullup_13 (.out(diodebackward_35_out));
  not not_14 (nCRES, diodebackward_35_out);
  DiodeBackward diodebackward_43 (.in(nS0), .out(diodebackward_30_out));
  PullUp pullup_14 (.out(diodebackward_30_out));
  PullUp pullup_15 (.out(nC));
  DiodeBackward diodebackward_44 (.in(SUB), .out(diodebackward_44_out));
  DiodeBackward diodebackward_45 (.in(SUB), .out(nC));
  nand nand_13 (nand_13_out, 1'b1, nand_16_out, nand_14_out);
  nand nand_14 (nand_14_out, nand_13_out, GCLK, nRESET);
  nand nand_15 (nand_15_out, nand_14_out, GCLK, nand_16_out);
  nand nand_16 (nand_16_out, nand_15_out, nand_45_out[3], nRESET);
  nand nand_17 (nand_17_out, 1'b1, nand_20_out, nand_18_out);
  nand nand_18 (nand_18_out, nand_17_out, GCLK, CLR);
  nand nand_19 (nand_19_out, nand_18_out, GCLK, nand_20_out);
  nand nand_20 (nand_20_out, nand_19_out, nand_47_out[3], CLR);
  DiodeBackward diodebackward_46 (.in(1'b1), .out(diodebackward_46_out));
  PullUp pullup_16 (.out(diodebackward_44_out));
  DiodeBackward diodebackward_47 (.in(S2), .out(diodebackward_46_out));
  DiodeBackward diodebackward_48 (.in(nS1), .out(diodebackward_46_out));
  PullUp pullup_17 (.out(pullup_17_out));
  PullUp pullup_18 (.out(pullup_18_out));
  DiodeBackward diodebackward_49 (.in(AND), .out(pullup_18_out));
  DiodeBackward diodebackward_50 (.in(OR), .out(pullup_18_out));
  nand nand_21 (nand_45_out[2], 1'b1, nand_14_out, nand_22_out);
  nand nand_22 (nand_22_out, nand_45_out[2], nand_15_out, nRESET);
  nand nand_23 (nand_47_out[2], 1'b1, nand_18_out, nand_24_out);
  nand nand_24 (nand_24_out, nand_47_out[2], nand_19_out, CLR);
  DiodeBackward diodebackward_51 (.in(D5), .out(diodebackward_46_out));
  DiodeBackward diodebackward_52 (.in(S0), .out(diodebackward_46_out));
  PullUp pullup_19 (.out(pullup_19_out));
  DiodeBackward diodebackward_53 (.in(LOAD), .out(pullup_19_out));
  DiodeBackward diodebackward_54 (.in(OR), .out(pullup_19_out));
  DiodeBackward diodebackward_55 (.in(XOR), .out(pullup_19_out));
  DiodeBackward diodebackward_56 (.in(ADD), .out(pullup_19_out));
  DiodeBackward diodebackward_57 (.in(SUB), .out(pullup_19_out));
  DiodeBackward diodebackward_58 (.in(ST), .out(pullup_19_out));
  not not_15 (I0, pullup_19_out);
  not not_16 (I1, pullup_18_out);
  not not_17 (nA, pullup_17_out);
  not not_18 (nB, diodebackward_44_out);
  not not_19 (C_t, nC);
  not not_20 (F, pullup_10_out);
  not not_21 (CLA, diodebackward_32_out);
  PullUp pullup_20 (.out(pullup_20_out));
  DiodeBackward diodebackward_59 (.in(CLA), .out(pullup_20_out));
  DiodeBackward diodebackward_60 (.in(LD_t), .out(pullup_20_out));
  DiodeBackward diodebackward_61 (.in(1'b1), .out(diodebackward_61_out));
  PullUp pullup_21 (.out(diodebackward_46_out));
  not not_22 (CLR, pullup_20_out);
  DiodeBackward diodebackward_62 (.in(S2), .out(diodebackward_61_out));
  DiodeBackward diodebackward_63 (.in(nS1), .out(diodebackward_61_out));
  DiodeForward diodeforward_1 (.in(diodebackward_30_out), .out(diodeforward_1_out));
  DiodeForward diodeforward_2 (.in(diodebackward_25_out), .out(diodeforward_1_out));
  PullDown pulldown_1 (.out(diodeforward_1_out));
  DiodeBackward diodebackward_64 (.in(D4), .out(diodebackward_61_out));
  DiodeBackward diodebackward_65 (.in(nS0), .out(diodebackward_61_out));
  DiodeForward diodeforward_3 (.in(diodebackward_61_out), .out(diodeforward_1_out));
  DiodeForward diodeforward_4 (.in(diodebackward_46_out), .out(diodeforward_1_out));
  nand nand_25 (nand_25_out, 1'b1, nand_28_out, nand_26_out);
  nand nand_26 (nand_26_out, nand_25_out, GCLK, nRESET);
  nand nand_27 (nand_27_out, nand_26_out, GCLK, nand_28_out);
  nand nand_28 (nand_28_out, nand_27_out, nand_45_out[2], nRESET);
  nand nand_29 (nand_29_out, 1'b1, nand_32_out, nand_30_out);
  nand nand_30 (nand_30_out, nand_29_out, GCLK, CLR);
  nand nand_31 (nand_31_out, nand_30_out, GCLK, nand_32_out);
  nand nand_32 (nand_32_out, nand_31_out, nand_47_out[2], CLR);
  PullUp pullup_22 (.out(diodebackward_61_out));
  DiodeForward diodeforward_5 (.in(diodebackward_71_out), .out(diodeforward_1_out));
  DiodeForward diodeforward_6 (.in(diodebackward_66_out), .out(diodeforward_1_out));
  DiodeBackward diodebackward_66 (.in(nS2), .out(diodebackward_66_out));
  DiodeBackward diodebackward_67 (.in(1'b1), .out(diodebackward_66_out));
  DiodeForward diodeforward_7 (.in(diodebackward_85_out), .out(diodeforward_1_out));
  DiodeForward diodeforward_8 (.in(diodebackward_80_out), .out(diodeforward_1_out));
  nand nand_33 (nand_45_out[1], 1'b1, nand_26_out, nand_34_out);
  nand nand_34 (nand_34_out, nand_45_out[1], nand_27_out, nRESET);
  nand nand_35 (nand_47_out[1], 1'b1, nand_30_out, nand_36_out);
  nand nand_36 (nand_36_out, nand_47_out[1], nand_31_out, CLR);
  DiodeBackward diodebackward_68 (.in(D3), .out(diodebackward_66_out));
  DiodeBackward diodebackward_69 (.in(S1), .out(diodebackward_66_out));
  not not_23 (not_23_out, diodeforward_1_out);
  Monoflop monoflop_1 (.C(LD), .R(1'b0), .Q(SETC), .nQ(RES));
  Monoflop monoflop_2 (.C(button_1_out), .R(1'b0), .Q(LD_t), .nQ(LD));
  Button button_1 (.out(button_1_out));
  DiodeBackward diodebackward_70 (.in(S0), .out(diodebackward_66_out));
  PullUp pullup_23 (.out(diodebackward_66_out));
  Reset reset_1 (.out(nRESET));
  DiodeBackward diodebackward_71 (.in(nS2), .out(diodebackward_71_out));
  DiodeBackward diodebackward_72 (.in(1'b1), .out(diodebackward_71_out));
  not not_24 (not_24_out, not_23_out);
  nand nand_37 (nand_37_out, 1'b1, nand_40_out, nand_38_out);
  nand nand_38 (nand_38_out, nand_37_out, GCLK, nRESET);
  nand nand_39 (nand_39_out, nand_38_out, GCLK, nand_40_out);
  nand nand_40 (nand_40_out, nand_39_out, nand_45_out[1], nRESET);
  nand nand_41 (nand_41_out, 1'b1, nand_44_out, nand_42_out);
  nand nand_42 (nand_42_out, nand_41_out, GCLK, CLR);
  nand nand_43 (nand_43_out, nand_42_out, GCLK, nand_44_out);
  nand nand_44 (nand_44_out, nand_43_out, nand_47_out[1], CLR);
  DiodeBackward diodebackward_73 (.in(D2), .out(diodebackward_71_out));
  DiodeBackward diodebackward_74 (.in(S1), .out(diodebackward_71_out));
  DiodeBackward diodebackward_75 (.in(not_24_out), .out(diodebackward_75_out));
  DiodeBackward diodebackward_76 (.in(not_25_out), .out(diodebackward_75_out));
  not not_25 (not_25_out, nB);
  DiodeBackward diodebackward_77 (.in(not_23_out), .out(diodebackward_77_out));
  DiodeBackward diodebackward_78 (.in(nB), .out(diodebackward_77_out));
  DiodeBackward diodebackward_79 (.in(nS0), .out(diodebackward_71_out));
  PullUp pullup_24 (.out(diodebackward_71_out));
  PullUp pullup_25 (.out(diodebackward_75_out));
  PullUp pullup_26 (.out(diodebackward_77_out));
  nand nand_45 (nand_45_out[0], 1'b1, nand_38_out, nand_46_out);
  nand nand_46 (nand_46_out, nand_45_out[0], nand_39_out, nRESET);
  nand nand_47 (nand_47_out[0], 1'b1, nand_42_out, nand_48_out);
  nand nand_48 (nand_48_out, nand_47_out[0], nand_43_out, CLR);
  DiodeBackward diodebackward_80 (.in(1'b1), .out(diodebackward_80_out));
  not not_26 (not_26_out, diodeforward_9_out);
  DiodeForward diodeforward_9 (.in(diodebackward_75_out), .out(diodeforward_9_out));
  DiodeForward diodeforward_10 (.in(diodebackward_77_out), .out(diodeforward_9_out));
  PullDown pulldown_2 (.out(diodeforward_9_out));
  DiodeBackward diodebackward_81 (.in(nS2), .out(diodebackward_80_out));
  DiodeBackward diodebackward_82 (.in(nS1), .out(diodebackward_80_out));
  not not_27 (Bin, not_26_out);
  LED led_1 (.in(D7));
  D_FF IC16 (.D(IC16_nq), .C(button_2_out), .Q(D7), .nQ(IC16_nq));
  Button button_2 (.out(button_2_out));
  DiodeBackward diodebackward_83 (.in(D1), .out(diodebackward_80_out));
  DiodeBackward diodebackward_84 (.in(S0), .out(diodebackward_80_out));
  LED led_2 (.in(D6));
  D_FF d_ff_1 (.D(d_ff_1_nq), .C(button_3_out), .Q(D6), .nQ(d_ff_1_nq));
  Button button_3 (.out(button_3_out));
  DiodeBackward diodebackward_85 (.in(1'b1), .out(diodebackward_85_out));
  PullUp pullup_27 (.out(diodebackward_80_out));
  LED led_3 (.in(D5));
  D_FF d_ff_2 (.D(d_ff_2_nq), .C(button_4_out), .Q(D5), .nQ(d_ff_2_nq));
  Button button_4 (.out(button_4_out));
  DiodeBackward diodebackward_86 (.in(nS2), .out(diodebackward_85_out));
  DiodeBackward diodebackward_87 (.in(nS1), .out(diodebackward_85_out));
  LED led_4 (.in(D4));
  D_FF d_ff_3 (.D(d_ff_3_nq), .C(button_5_out), .Q(D4), .nQ(d_ff_3_nq));
  Button button_5 (.out(button_5_out));
  nand nand_49 (nand_49_out, 1'b1, nand_52_out, nand_50_out);
  nand nand_50 (nand_50_out, nand_49_out, GCLK, nRESET);
  nand nand_51 (nand_51_out, nand_50_out, GCLK, nand_52_out);
  nand nand_52 (nand_52_out, nand_51_out, nand_45_out[0], nRESET);
  nand nand_53 (nand_53_out, 1'b1, nand_56_out, nand_54_out);
  nand nand_54 (nand_54_out, nand_53_out, GCLK, CLR);
  nand nand_55 (nand_55_out, nand_54_out, GCLK, nand_56_out);
  nand nand_56 (nand_56_out, nand_55_out, nand_47_out[0], CLR);
  DiodeBackward diodebackward_88 (.in(D0), .out(diodebackward_85_out));
  DiodeBackward diodebackward_89 (.in(nS0), .out(diodebackward_85_out));
  LED led_5 (.in(D3));
  D_FF d_ff_4 (.D(d_ff_4_nq), .C(button_6_out), .Q(D3), .nQ(d_ff_4_nq));
  Button button_6 (.out(button_6_out));
  PullUp pullup_28 (.out(diodebackward_85_out));
  LED led_6 (.in(D2));
  D_FF d_ff_5 (.D(d_ff_5_nq), .C(button_7_out), .Q(D2), .nQ(d_ff_5_nq));
  Button button_7 (.out(button_7_out));
  nand nand_57 (nand_57_out[3], 1'b1, nand_50_out, nand_58_out);
  nand nand_58 (nand_58_out, nand_57_out[3], nand_51_out, nRESET);
  nand nand_59 (nand_59_out[3], 1'b1, nand_54_out, nand_60_out);
  nand nand_60 (nand_60_out, nand_59_out[3], nand_55_out, CLR);
  LED led_7 (.in(D1));
  D_FF d_ff_6 (.D(d_ff_6_nq), .C(button_8_out), .Q(D1), .nQ(d_ff_6_nq));
  Button button_8 (.out(button_8_out));
  nand nand_61 (nand_61_out, clk, clk);
  nand nand_62 (GATE, RES, nGATE);
  nand nand_63 (nGATE, GATE, T0);
  LED led_8 (.in(D0));
  D_FF IC16_2 (.D(IC16_2_nq), .C(button_9_out), .Q(D0), .nQ(IC16_2_nq));
  Button button_9 (.out(button_9_out));
  Seven_Seg_Hex seven_seg_hex_1 (.d({D7, D6, D5, D4}), .dp(1'b0));
  nand nand_64 (GCLK, nand_61_out, GATE);
  Seven_Seg_Hex seven_seg_hex_2 (.d({D3, D2, D1, D0}), .dp(1'b0));
  nand nand_65 (nand_65_out, 1'b1, nand_68_out, nand_66_out);
  nand nand_66 (nand_66_out, nand_65_out, GCLK, nRESET);
  nand nand_67 (nand_67_out, nand_66_out, GCLK, nand_68_out);
  nand nand_68 (nand_68_out, nand_67_out, nand_57_out[3], nRESET);
  nand nand_69 (nand_69_out, 1'b1, nand_72_out, nand_70_out);
  nand nand_70 (nand_70_out, nand_69_out, GCLK, CLR);
  nand nand_71 (nand_71_out, nand_70_out, GCLK, nand_72_out);
  nand nand_72 (nand_72_out, nand_71_out, nand_59_out[3], CLR);
  nand nand_73 (nand_57_out[2], 1'b1, nand_66_out, nand_74_out);
  nand nand_74 (nand_74_out, nand_57_out[2], nand_67_out, nRESET);
  nand nand_75 (nand_59_out[2], 1'b1, nand_70_out, nand_76_out);
  nand nand_76 (nand_76_out, nand_59_out[2], nand_71_out, CLR);
  nand nand_77 (nand_77_out, 1'b1, nand_80_out, nand_78_out);
  nand nand_78 (nand_78_out, nand_77_out, clk, GATE);
  nand nand_79 (nand_79_out, nand_78_out, clk, nand_80_out);
  nand nand_80 (nand_80_out, nand_79_out, nS0, GATE);
  nand nand_81 (nand_81_out, 1'b1, nand_84_out, nand_82_out);
  nand nand_82 (nand_82_out, nand_81_out, GCLK, nRESET);
  nand nand_83 (nand_83_out, nand_82_out, GCLK, nand_84_out);
  nand nand_84 (nand_84_out, nand_83_out, nand_57_out[2], nRESET);
  nand nand_85 (nand_85_out, 1'b1, nand_88_out, nand_86_out);
  nand nand_86 (nand_86_out, nand_85_out, GCLK, CLR);
  nand nand_87 (nand_87_out, nand_86_out, GCLK, nand_88_out);
  nand nand_88 (nand_88_out, nand_87_out, nand_59_out[2], CLR);
  PullUp pullup_29 (.out(pullup_29_out));
  DiodeBackward diodebackward_90 (.in(Aout), .out(pullup_29_out));
  DiodeBackward diodebackward_91 (.in(C), .out(pullup_29_out));
  DiodeBackward diodebackward_92 (.in(Bin), .out(diodebackward_92_out));
  DiodeBackward diodebackward_93 (.in(C), .out(diodebackward_92_out));
  DiodeBackward diodebackward_94 (.in(Cin), .out(diodebackward_94_out));
  DiodeBackward diodebackward_95 (.in(C), .out(diodebackward_94_out));
  DiodeBackward diodebackward_96 (.in(Aout), .out(diodebackward_96_out));
  DiodeBackward diodebackward_97 (.in(Bin), .out(diodebackward_96_out));
  DiodeBackward diodebackward_98 (.in(Cin), .out(diodebackward_96_out));
  PullUp pullup_30 (.out(pullup_30_out));
  DiodeBackward diodebackward_99 (.in(Aout), .out(pullup_30_out));
  DiodeBackward diodebackward_100 (.in(Bin), .out(pullup_30_out));
  DiodeBackward diodebackward_101 (.in(Aout), .out(diodebackward_101_out));
  DiodeBackward diodebackward_102 (.in(Cin), .out(diodebackward_101_out));
  DiodeBackward diodebackward_103 (.in(Bin), .out(diodebackward_103_out));
  DiodeBackward diodebackward_104 (.in(Cin), .out(diodebackward_103_out));
  nand nand_89 (S0, 1'b1, nand_78_out, nS0);
  nand nand_90 (nS0, S0, nand_79_out, GATE);
  PullUp pullup_31 (.out(diodebackward_92_out));
  PullUp pullup_32 (.out(diodebackward_94_out));
  PullUp pullup_33 (.out(diodebackward_101_out));
  PullUp pullup_34 (.out(diodebackward_103_out));
  nand nand_91 (nand_57_out[1], 1'b1, nand_82_out, nand_92_out);
  nand nand_92 (nand_92_out, nand_57_out[1], nand_83_out, nRESET);
  nand nand_93 (nand_59_out[1], 1'b1, nand_86_out, nand_94_out);
  nand nand_94 (nand_94_out, nand_59_out[1], nand_87_out, CLR);
  PullUp pullup_35 (.out(diodebackward_96_out));
  DiodeForward diodeforward_11 (.in(pullup_29_out), .out(diodeforward_11_out));
  DiodeForward diodeforward_12 (.in(diodebackward_92_out), .out(diodeforward_11_out));
  DiodeForward diodeforward_13 (.in(diodebackward_94_out), .out(diodeforward_11_out));
  DiodeForward diodeforward_14 (.in(diodebackward_96_out), .out(diodeforward_11_out));
  DiodeForward diodeforward_15 (.in(pullup_30_out), .out(diodeforward_15_out));
  DiodeForward diodeforward_16 (.in(diodebackward_101_out), .out(diodeforward_15_out));
  DiodeForward diodeforward_17 (.in(diodebackward_103_out), .out(diodeforward_15_out));
  nand nand_95 (nand_95_out, 1'b1, nand_98_out, nand_96_out);
  nand nand_96 (nand_96_out, nand_95_out, nS0, GATE);
  nand nand_97 (nand_97_out, nand_96_out, nS0, nand_98_out);
  nand nand_98 (nand_98_out, nand_97_out, nS1, GATE);
  PullDown pulldown_3 (.out(diodeforward_11_out));
  PullDown pulldown_4 (.out(diodeforward_15_out));
  not not_28 (S, diodeforward_11_out);
  not not_29 (C, diodeforward_15_out);
  nand nand_99 (nand_99_out, 1'b1, nand_102_out, nand_100_out);
  nand nand_100 (nand_100_out, nand_99_out, GCLK, nRESET);
  nand nand_101 (nand_101_out, nand_100_out, GCLK, nand_102_out);
  nand nand_102 (nand_102_out, nand_101_out, nand_57_out[1], nRESET);
  nand nand_103 (nand_103_out, 1'b1, nand_106_out, nand_104_out);
  nand nand_104 (nand_104_out, nand_103_out, GCLK, CLR);
  nand nand_105 (nand_105_out, nand_104_out, GCLK, nand_106_out);
  nand nand_106 (nand_106_out, nand_105_out, nand_59_out[1], CLR);
  nand nand_107 (S1, 1'b1, nand_96_out, nS1);
  nand nand_108 (nS1, S1, nand_97_out, GATE);
  not not_30 (Sum, S);
  not not_31 (Cout, C);
  nand nand_109 (PCout, 1'b1, nand_100_out, nand_110_out);
  nand nand_110 (nand_110_out, PCout, nand_101_out, nRESET);
  nand nand_111 (Aout, 1'b1, nand_104_out, nand_112_out);
  nand nand_112 (nand_112_out, Aout, nand_105_out, CLR);
  nand nand_113 (nand_113_out, 1'b1, nand_116_out, nand_114_out);
  nand nand_114 (nand_114_out, nand_113_out, nS1, GATE);
  nand nand_115 (nand_115_out, nand_114_out, nS1, nand_116_out);
  nand nand_116 (nand_116_out, nand_115_out, nS2, GATE);
  Seven_Seg_Hex seven_seg_hex_3 (.d(nand_45_out), .dp(1'b0));
  Seven_Seg_Hex seven_seg_hex_4 (.d(nand_47_out), .dp(1'b0));
  nand nand_117 (S2, 1'b1, nand_114_out, nS2);
  nand nand_118 (nS2, S2, nand_115_out, GATE);
  DiodeBackward diodebackward_105 (.in(Sum), .out(diodebackward_105_out));
  DiodeBackward diodebackward_106 (.in(I0), .out(diodebackward_105_out));
  DiodeBackward diodebackward_107 (.in(I1), .out(diodebackward_107_out));
  DiodeBackward diodebackward_108 (.in(Cout), .out(diodebackward_107_out));
  Seven_Seg_Hex seven_seg_hex_5 (.d({nand_57_out, PCout}), .dp(1'b0));
  Seven_Seg_Hex seven_seg_hex_6 (.d({nand_59_out, Aout}), .dp(1'b0));
  PullUp pullup_36 (.out(diodebackward_105_out));
  PullUp pullup_37 (.out(diodebackward_107_out));
  DiodeBackward diodebackward_109 (.in(Cout), .out(diodebackward_109_out));
  DiodeBackward diodebackward_110 (.in(F), .out(diodebackward_109_out));
  DiodeForward diodeforward_18 (.in(diodebackward_105_out), .out(diodeforward_18_out));
  DiodeForward diodeforward_19 (.in(diodebackward_107_out), .out(diodeforward_18_out));
  PullUp pullup_38 (.out(diodebackward_109_out));
  not not_32 (not_32_out, diodebackward_109_out);
  nand nand_119 (nand_119_out, 1'b1, nand_122_out, nand_120_out);
  nand nand_120 (nand_120_out, nand_119_out, nS2, GATE);
  nand nand_121 (nand_121_out, nand_120_out, nS2, nand_122_out);
  nand nand_122 (nand_122_out, nand_121_out, nand_124_out, GATE);
  not not_33 (not_33_out, diodeforward_18_out);
  PullDown pulldown_5 (.out(diodeforward_18_out));
  DiodeBackward diodebackward_111 (.in(not_32_out), .out(diodebackward_111_out));
  not not_34 (Fout, not_33_out);
  PullUp pullup_39 (.out(diodebackward_111_out));
  not not_35 (Cout_t, diodebackward_111_out);
  not not_36 (not_36_out, PCout);
  not not_37 (not_37_out, PC_Cin);
  not not_38 (not_38_out, nJMP);
  nand nand_123 (nand_123_out[3], 1'b1, nand_120_out, nand_124_out);
  nand nand_124 (nand_124_out, nand_123_out[3], nand_121_out, GATE);
  DiodeBackward diodebackward_112 (.in(not_36_out), .out(diodebackward_112_out));
  DiodeBackward diodebackward_113 (.in(PC_Cin), .out(diodebackward_112_out));
  DiodeBackward diodebackward_114 (.in(not_37_out), .out(diodebackward_114_out));
  DiodeBackward diodebackward_115 (.in(PCout), .out(diodebackward_114_out));
  DiodeBackward diodebackward_116 (.in(PC_Cin), .out(diodebackward_116_out));
  DiodeBackward diodebackward_117 (.in(PCout), .out(diodebackward_116_out));
  DiodeBackward diodebackward_118 (.in(PC_S), .out(diodebackward_118_out));
  DiodeBackward diodebackward_119 (.in(nJMP), .out(diodebackward_118_out));
  DiodeBackward diodebackward_120 (.in(not_38_out), .out(diodebackward_120_out));
  DiodeBackward diodebackward_121 (.in(Bin), .out(diodebackward_120_out));
  PullUp pullup_40 (.out(diodebackward_112_out));
  PullUp pullup_41 (.out(diodebackward_114_out));
  PullUp pullup_42 (.out(diodebackward_116_out));
  PullUp pullup_43 (.out(diodebackward_118_out));
  PullUp pullup_44 (.out(diodebackward_120_out));
  nand nand_125 (nand_125_out, S1, S0, S2);
  DiodeForward diodeforward_20 (.in(diodebackward_112_out), .out(diodeforward_20_out));
  DiodeForward diodeforward_21 (.in(diodebackward_114_out), .out(diodeforward_20_out));
  DiodeForward diodeforward_22 (.in(diodebackward_116_out), .out(diodeforward_22_out));
  Seven_Seg_Hex seven_seg_hex_7 (.d({nand_123_out[3], S2, S1, S0}), .dp(1'b0));
  PullDown pulldown_6 (.out(diodeforward_20_out));
  PullDown pulldown_7 (.out(diodeforward_22_out));
  not not_39 (not_39_out, diodeforward_23_out);
  DiodeForward diodeforward_23 (.in(diodebackward_118_out), .out(diodeforward_23_out));
  DiodeForward diodeforward_24 (.in(diodebackward_120_out), .out(diodeforward_23_out));
  PullDown pulldown_8 (.out(diodeforward_23_out));
  not not_40 (RCO, nand_125_out);
  not not_41 (not_41_out, GCLK);
  not not_42 (not_42_out, not_41_out);
  _74595 U4 (
    .pin1(BUS6), .pin2(BUS5), .pin3(BUS4), .pin4(BUS3), .pin5(BUS2), .pin6(BUS1), .pin7(BUS0), .pin8(1'b0),
    .pin9(U4_pin9), .pin10(RES), .pin11(GCLK), .pin12(T0), .pin13(1'b0), .pin14(Bin), .pin15(BUS7),
    .pin16(1'b1));
  not not_43 (not_43_out, diodeforward_20_out);
  not not_44 (not_44_out, diodeforward_22_out);
  not not_45 (PCin, not_39_out);
  not not_46 (PC_S, not_43_out);
  not not_47 (PC_Cout, not_44_out);
  nand nand_126 (nand_126_out, nCSET, nand_129_out, nand_127_out);
  nand nand_127 (nand_127_out, nand_126_out, not_42_out, nCRES);
  nand nand_128 (nand_128_out, nand_127_out, not_42_out, nand_129_out);
  nand nand_129 (nand_129_out, nand_128_out, Cout_t, nCRES);
  nand nand_130 (Cin, nCSET, nand_127_out, nand_131_out);
  nand nand_131 (nand_131_out, Cin, nand_128_out, nCRES);
  DiodeForward diodeforward_25 (.in(BUS7), .out(diodeforward_25_out));
  DiodeForward diodeforward_26 (.in(BUS6), .out(diodeforward_25_out));
  DiodeForward diodeforward_27 (.in(BUS5), .out(diodeforward_25_out));
  DiodeForward diodeforward_28 (.in(BUS4), .out(diodeforward_25_out));
  DiodeForward diodeforward_29 (.in(BUS3), .out(diodeforward_25_out));
  DiodeForward diodeforward_30 (.in(BUS2), .out(diodeforward_25_out));
  DiodeForward diodeforward_31 (.in(BUS1), .out(diodeforward_25_out));
  DiodeForward diodeforward_32 (.in(BUS0), .out(diodeforward_25_out));
  not not_48 (not_48_out, LD_t);
  Seven_Seg_Hex seven_seg_hex_8 (.d({BUS7, BUS6, BUS5, BUS4}), .dp(1'b0));
  nand nand_132 (ZERO, diodeforward_25_out, diodeforward_25_out);
  PullDown pulldown_9 (.out(diodeforward_25_out));
  nand nand_133 (nand_133_out, not_48_out, nand_136_out, nand_134_out);
  nand nand_134 (nand_134_out, nand_133_out, clk, nRESET);
  nand nand_135 (nand_135_out, nand_134_out, clk, nand_136_out);
  nand nand_136 (nand_136_out, nand_135_out, PC_Cout, nRESET);
  Seven_Seg_Hex seven_seg_hex_9 (.d({BUS3, BUS2, BUS1, BUS0}), .dp(1'b0));
  LED led_9 (.in(ZERO));
  nand nand_137 (PC_Cin, not_48_out, nand_134_out, nand_138_out);
  nand nand_138 (nand_138_out, PC_Cin, nand_135_out, nRESET);
  nand nand_139 (nand_139_out, 1'b1, nand_142_out, nand_140_out);
  nand nand_140 (nand_140_out, nand_139_out, clk, 1'b1);
  nand nand_141 (nand_141_out, nand_140_out, clk, nand_142_out);
  nand nand_142 (nand_142_out, nand_141_out, RCO, 1'b1);
  nand nand_143 (IX, 1'b1, nand_140_out, T0);
  nand nand_144 (T0, IX, nand_141_out, 1'b1);

  // Other names for the same wires on the sheet: Cy = Cout; IR4 = in_2; IR5 = in_3; IR6 = in_4; nLOAD = LD;
  //   nRES = RES; RST = GATE; S_t = Sum

  // Notes on the sheet:
  //   clk: Hz: 2147483647
  //   MITE
  //   INSTRUCTION DECODER
  //   8:1 Data Selector
  //   8-bit Serialiser B
  //   Detect 000
  //   Detect 001
  //   Detect 010
  //   Detect 011
  //   Detect 100
  //   Detect 101
  //   Detect 110
  //   Detect 111
  //   1
  //   3
  //   4
  //   6
  //   2
  //   5
  //   CLA
  //   Instruction Decoder
  //   F
  //   C
  //   ~B
  //   I1
  //   ~A
  //   I0
  //   LOAD
  //   AND
  //   OR
  //   XOR
  //   ADD
  //   SUB
  //   STORE
  //   JMP
  //   Instruction Input
  //   Enter 3-bit Instruction
  //   STEP/RUN
  //   MITE 8-bit  Bit serial CPU Testbed
  //   100 = ADD
  //   101 = SUB
  //   ENTER L
  //   Data Input
  //   ALU
  //   Shift Register A
  //   DTL Adder using AND-OR-INVERT
  //   S=(A.~C)+(B.~C)+(Cin.~C)+(A.B.Cin)
  //   C=(A.B)+(A.Cin)+(B.Cin)
  //   Clock Sequencer
  //   PROGRAM COUNTER
  //   ACCUMULATOR
  //   ALU Multiplexer
  //   DTL Half Adder using AND-OR-INVERT
  //   Suppress Carry
  //   # Clock
  //   Output Display Register
  //   S=(A.~C)+(~A.C)
  //   PC-C=(PC_out.PC_Cin)
  //   Carry FF
  //   Any residual carry is cleared before an operation
  //   PC FF
  //   Carry is only set before Bit 0 of an operation
  //   OUTPUT REGISTER
  //   PC Carry FF
  //   Carry is  set on timeslot T0 of an operation
  //   ZERO
  //   Counter FF
endmodule
